# Fritzing sketch Versuch 1 (saved by Fritzing 0.9.6b)
breadboards: 1

parts:
  VCC1 = Battery block 9V
  R1 = Resistor [tolerance=±5% power=0.25 resistance=10k package=THT]
  LED3 = LED - 5mm [color="Green (560nm)" current=0.030 package="5 mm [THT]"]

nets:
  N1: VCC1.-, LED3.cathode
  N2: VCC1.+, R1.Pin_0
  N3: R1.Pin_1, LED3.anode
