# Fritzing sketch Versuch 11 (saved by Fritzing 0.9.6b)
breadboards: 1

parts:
  VCC1 = Battery block 9V
  CD4048B1 = CD4048B [part_number=CD4046BE package="DIP (Dual Inline) [THT]"]
  LED2 = LED - 5mm [color="Green (565nm)" current=0.030 package="5 mm [THT]"]
  C2 = Ceramic Capacitor [capacitance="100 nF" voltage=35V package="0805 [SMD, multilayer]"]
  R2 = Resistor [tolerance=±5% resistance=100k package="2010 [SMD]"]
  J2 = Piezo Speaker
  R3 = Vertical Resistor [tolerance=±5% resistance=10k package=THT]
  LED6 = LED - 5mm [color="Red (635nm)" current=0.030 package="5 mm [THT]"]
  R4 = Vertical Resistor [tolerance=±5% resistance=10k package=THT]
  R5 = Vertical Resistor [tolerance=±5% resistance=1M package=THT]
  C8 = Ceramic Capacitor [capacitance="100 nF" voltage=35V package="1206 [SMD, multilayer]"]

nets:
  N1: VCC1.-, CD4048B1.F, CD4048B1.VSS, R2.Pin_1, J2.pin1, R3.Pin_1, R4.Pin_1
  N2: VCC1.+, CD4048B1.VDD, LED2.anode, LED6.anode, C8.1
  N3: CD4048B1.G, J2.pin2
  N4: CD4048B1.E, C2.1
  N5: CD4048B1.Kb, C2.0
  N6: CD4048B1.Kc, R5.Pin_0, C8.0
  N7: CD4048B1.D, R3.Pin_0
  N8: CD4048B1.C, R2.Pin_0
  N9: LED2.cathode, LED6.cathode, R4.Pin_0, R5.Pin_1

custom parts:
  CD4048B: CMOS Multifunction Expandable 8-Input Gate
  Vertical Resistor: A generic resistor (0.25W)
