# Fritzing sketch Versuch 13 (saved by Fritzing 0.9.6b)
breadboards: 1

parts:
  VCC1 = Battery block 9V
  CD4048B1 = CD4048B [part_number=CD4046BE package="DIP (Dual Inline) [THT]"]
  C2 = Ceramic Capacitor [capacitance="100 nF" voltage=35V package="0805 [SMD, multilayer]"]
  J1 = Piezo Speaker
  C3 = Ceramic Capacitor [capacitance="100 nF" voltage=35V package="1206 [SMD, multilayer]"]
  R2 = Vertical Resistor [tolerance=±5% resistance=10k package=THT]
  R3 = Vertical Resistor [tolerance=±5% resistance=100k package=THT]

nets:
  N1: VCC1.-, CD4048B1.F, CD4048B1.VSS, J1.pin1, C3.1, R2.Pin_1, R3.Pin_1
  N2: VCC1.+, CD4048B1.VDD
  N3: CD4048B1.G, J1.pin2
  N4: CD4048B1.E, C2.1
  N5: CD4048B1.Kb, C2.0
  N6: CD4048B1.Kc, C3.0
  N7: CD4048B1.D, R2.Pin_0
  N8: CD4048B1.C, R3.Pin_0

custom parts:
  CD4048B: CMOS Multifunction Expandable 8-Input Gate
  Vertical Resistor: A generic resistor (0.25W)
