# Fritzing sketch Versuch 16 (saved by Fritzing 0.9.6b)
breadboards: 1

parts:
  VCC1 = Battery block 9V
  CD4048B1 = CD4048B [part_number=CD4046BE package="DIP (Dual Inline) [THT]"]
  C2 = Ceramic Capacitor [capacitance="100 nF" voltage=35V package="0805 [SMD, multilayer]"]
  R2 = Resistor [tolerance=±5% resistance=10k package="2010 [SMD]"]
  J2 = Piezo Speaker
  R3 = Vertical Resistor [tolerance=±5% resistance=10k package=THT]
  R4 = Vertical Resistor [tolerance=±5% resistance=10M package=THT]
  Q1 = Transistor Top View [package="TO92 [THT] Top"]
  R5 = Vertical Resistor [tolerance=±5% resistance=10k package=THT]
  LED1 = LED - 5mm [color="Blue (505nm)" current=0.030 package="5 mm [THT]"]

nets:
  N1: VCC1.-, CD4048B1.F, CD4048B1.VSS, R2.Pin_1, J2.pin1, Q1.3, LED1.cathode
  N2: VCC1.+, CD4048B1.VDD, R3.Pin_0, R4.Pin_0
  N3: CD4048B1.G, J2.pin2
  N4: CD4048B1.E, C2.1
  N5: CD4048B1.Kb, C2.0
  N6: CD4048B1.Kc, R3.Pin_1, Q1.1
  N7: CD4048B1.Ka, R5.Pin_1
  N8: CD4048B1.D, R2.Pin_0
  N9: R4.Pin_1, Q1.2
  N10: R5.Pin_0, LED1.anode

custom parts:
  CD4048B: CMOS Multifunction Expandable 8-Input Gate
  Vertical Resistor: A generic resistor (0.25W)
  Transistor Top View: A standard transistor
