# Fritzing sketch Versuch 17 (saved by Fritzing 0.9.6b)
breadboards: 1

parts:
  VCC1 = Battery block 9V
  CD4048B1 = CD4048B [part_number=CD4046BE package="DIP (Dual Inline) [THT]"]
  C2 = Ceramic Capacitor [capacitance="100 nF" voltage=35V package="0805 [SMD, multilayer]"]
  R2 = Resistor [tolerance=±5% resistance=1M package="2010 [SMD]"]
  R4 = Vertical Resistor [tolerance=±5% resistance=100k package=THT]
  Q1 = Transistor Top View [package="TO92 [THT] Top"]
  R5 = Vertical Resistor [tolerance=±5% resistance=1k package=THT]
  R6 = Vertical Resistor [tolerance=±5% resistance=10k package=THT]
  C3 = Electrolytic Capacitor [capacitance=1µF voltage=35V package="100 mil [THT, electrolytic]"]
  LED3 = LED - 5mm [color="Green (565nm)" current=0.030 package="5 mm [THT]"]
  LED4 = LED - 3mm [color="Yellow (585nm)" current=0.030 package="3 mm [THT]"]
  LED5 = LED - 3mm [color="White (6500K)" current=0.030 package="3 mm [THT]"]
  R7 = Vertical Resistor [tolerance=±5% resistance=10k package=THT]

nets:
  N1: VCC1.-, CD4048B1.F, CD4048B1.VSS, R2.Pin_1, Q1.3, LED3.cathode
  N2: VCC1.+, CD4048B1.Kc, CD4048B1.VDD, R4.Pin_0, LED5.anode, R7.Pin_0
  N3: CD4048B1.Kd, R6.Pin_1
  N4: CD4048B1.H, CD4048B1.G, R5.Pin_0
  N5: CD4048B1.E, C2.1
  N6: CD4048B1.Kb, C2.0
  N7: CD4048B1.D, R2.Pin_0
  N8: CD4048B1.A, C3.-
  N9: R4.Pin_1, Q1.1, C3.+
  N10: Q1.2, LED4.anode
  N11: R5.Pin_1, LED5.cathode
  N12: R6.Pin_0, LED3.anode
  N13: LED4.cathode, R7.Pin_1

custom parts:
  CD4048B: CMOS Multifunction Expandable 8-Input Gate
  Vertical Resistor: A generic resistor (0.25W)
  Transistor Top View: A standard transistor
