# Fritzing sketch Versuch 18 (saved by Fritzing 0.9.6b)
breadboards: 1

parts:
  VCC1 = Battery block 9V
  CD4048B1 = CD4048B [part_number=CD4046BE package="DIP (Dual Inline) [THT]"]
  C2 = Ceramic Capacitor [capacitance="100 nF" voltage=35V package="0805 [SMD, multilayer]"]
  C3 = Ceramic Capacitor [capacitance="100 nF" voltage=35V package="1206 [SMD, multilayer]"]
  R2 = Vertical Resistor [tolerance=±5% resistance=10000k package=THT]
  LED6 = LED - 5mm [color="Red (635nm)" current=0.030 package="5 mm [THT]"]
  LED7 = LED - 5mm [color="Green (565nm)" current=0.030 package="5 mm [THT]"]
  R3 = Vertical Resistor [tolerance=±5% resistance=10k package=THT]
  R4 = Vertical Resistor [tolerance=±5% resistance=10k package=THT]
  R5 = Vertical Resistor [tolerance=±5% resistance=10k package=THT]
  LED8 = LED - 5mm [color="Blue (505nm)" current=0.030 package="5 mm [THT]"]

nets:
  N1: VCC1.-, CD4048B1.F, CD4048B1.VSS, C3.1, R2.Pin_1, LED7.cathode, R4.Pin_1, LED8.cathode
  N2: VCC1.+, CD4048B1.VDD, LED6.anode
  N3: CD4048B1.Kd, R3.Pin_0
  N4: CD4048B1.H, CD4048B1.G, R5.Pin_1
  N5: CD4048B1.E, C2.1
  N6: CD4048B1.Kb, C2.0
  N7: CD4048B1.Kc, C3.0
  N8: CD4048B1.D, R2.Pin_0
  N9: CD4048B1.A, LED6.cathode, R4.Pin_0
  N10: LED7.anode, R5.Pin_0
  N11: R3.Pin_1, LED8.anode

custom parts:
  CD4048B: CMOS Multifunction Expandable 8-Input Gate
  Vertical Resistor: A generic resistor (0.25W)
