# Fritzing sketch Versuch 19 (saved by Fritzing 0.9.6b)
breadboards: 1

parts:
  VCC1 = Battery block 9V
  CD4048B1 = CD4048B [part_number=CD4046BE package="DIP (Dual Inline) [THT]"]
  LED2 = LED - 5mm [color="Green (565nm)" current=0.030 package="5 mm [THT]"]
  R1 = Resistor [tolerance=±5% power=0.25 resistance=10k package=THT]
  C2 = Ceramic Capacitor [capacitance="100 nF" voltage=35V package="0805 [SMD, multilayer]"]
  R2 = Resistor [tolerance=±5% resistance=10M package="2010 [SMD]"]
  LED8 = LED - 5mm [color="Red (635nm)" current=0.030 package="5 mm [THT]"]
  C4 = Ceramic Capacitor [capacitance="100 nF" voltage=35V package="1206 [SMD, multilayer]"]
  R3 = Vertical Resistor [tolerance=±5% resistance=10k package=THT]
  R4 = Vertical Resistor [tolerance=±5% resistance=10M package=THT]

nets:
  N1: VCC1.-, CD4048B1.F, CD4048B1.VSS, LED2.cathode, R2.Pin_1, C4.1, R3.Pin_1
  N2: VCC1.+, CD4048B1.VDD, LED8.anode
  N3: CD4048B1.Kd, R4.Pin_0
  N4: CD4048B1.H, CD4048B1.G, R1.Pin_1
  N5: CD4048B1.E, C2.1
  N6: CD4048B1.Kb, C2.0
  N7: CD4048B1.Kc, C4.0, R4.Pin_1
  N8: CD4048B1.D, R2.Pin_0
  N9: CD4048B1.A, LED8.cathode, R3.Pin_0
  N10: LED2.anode, R1.Pin_0

custom parts:
  CD4048B: CMOS Multifunction Expandable 8-Input Gate
  Vertical Resistor: A generic resistor (0.25W)
