# Fritzing sketch Versuch 21 (saved by Fritzing 0.9.6b)
breadboards: 1

parts:
  VCC1 = Battery block 9V
  CD4048B1 = CD4048B [part_number=CD4046BE package="DIP (Dual Inline) [THT]"]
  R2 = Resistor [tolerance=±5% power=0.25 resistance=10k package=THT]
  LED2 = LED - 5mm [color="Green (565nm)" current=0.030 package="5 mm [THT]"]
  Q1 = Transistor Top View [package="TO92 [THT] Top"]
  R3 = Vertical Resistor [tolerance=±5% resistance=100k package=THT]
  R4 = Vertical Resistor [tolerance=±5% resistance=10M package=THT]
  C2 = Electrolytic Capacitor [capacitance=1µF voltage=35V package="100 mil [THT, electrolytic]"]
  J2 = Piezo Speaker

nets:
  N1: VCC1.-, CD4048B1.H, CD4048B1.VSS, LED2.cathode, Q1.3, J2.pin1
  N2: VCC1.+, CD4048B1.VDD, R3.Pin_0
  N3: CD4048B1.Kd, R2.Pin_1, J2.pin2
  N4: CD4048B1.A, C2.-
  N5: R2.Pin_0, LED2.anode
  N6: Q1.1, R3.Pin_1, R4.Pin_0, C2.+
  N7: Q1.2, R4.Pin_1

custom parts:
  CD4048B: CMOS Multifunction Expandable 8-Input Gate
  Transistor Top View: A standard transistor
  Vertical Resistor: A generic resistor (0.25W)
