# Fritzing sketch Versuch 22 (saved by Fritzing 0.9.6b)
breadboards: 1

parts:
  VCC1 = Battery block 9V
  CD4048B1 = CD4048B [part_number=CD4046BE package="DIP (Dual Inline) [THT]"]
  Q1 = Transistor Top View [package="TO92 [THT] Top"]
  R3 = Vertical Resistor [tolerance=±5% resistance=100k package=THT]
  R4 = Vertical Resistor [tolerance=±5% resistance=10M package=THT]
  C2 = Electrolytic Capacitor [capacitance=1µF voltage=35V package="100 mil [THT, electrolytic]"]
  J2 = Piezo Speaker
  C5 = Ceramic Capacitor [capacitance="100 nF" voltage=35V package="1206 [SMD, multilayer]"]
  C6 = Ceramic Capacitor [capacitance="100 nF" voltage=35V package="0805 [SMD, multilayer]"]
  C7 = Electrolytic Capacitor [capacitance=1µF voltage=35V package="100 mil [THT, electrolytic]"]
  R5 = Vertical Resistor [tolerance=±5% resistance=10k package=THT]
  R6 = Vertical Resistor [tolerance=±5% resistance=100k package=THT]
  R7 = Vertical Resistor [tolerance=±5% resistance=100k package=THT]
  LED2 = LED - 5mm [color="Green (565nm)" current=0.030 package="5 mm [THT]"]
  C8 = Ceramic Capacitor [capacitance="100 nF" voltage=35V package="0805 [SMD, multilayer]"]

nets:
  N1: VCC1.-, CD4048B1.F, CD4048B1.VSS, Q1.3, J2.pin1, C5.1, C7.-, R7.Pin_1, LED2.cathode
  N2: VCC1.+, CD4048B1.VDD, R3.Pin_0
  N3: CD4048B1.Kd, R6.Pin_0
  N4: CD4048B1.H, CD4048B1.G, J2.pin2
  N5: CD4048B1.E, C6.1, C8.1
  N6: CD4048B1.Kb, C6.0, C8.0
  N7: CD4048B1.Kc, C5.0, R6.Pin_1
  N8: CD4048B1.Ka, R5.Pin_1
  N9: CD4048B1.D, R7.Pin_0
  N10: CD4048B1.A, C2.-
  N11: Q1.1, R3.Pin_1, R4.Pin_0, C2.+
  N12: Q1.2, R4.Pin_1
  N13: C7.+, R5.Pin_0, LED2.anode

custom parts:
  CD4048B: CMOS Multifunction Expandable 8-Input Gate
  Transistor Top View: A standard transistor
  Vertical Resistor: A generic resistor (0.25W)
