# Fritzing sketch Versuch 23 (saved by Fritzing 0.9.6b)
breadboards: 1

parts:
  VCC1 = Battery block 9V
  CD4048B1 = CD4048B [part_number=CD4046BE package="DIP (Dual Inline) [THT]"]
  Q1 = Transistor Top View [package="TO92 [THT] Top"]
  R3 = Vertical Resistor [tolerance=±5% resistance=100k package=THT]
  C2 = Electrolytic Capacitor [capacitance=1µF voltage=35V package="100 mil [THT, electrolytic]"]
  J2 = Piezo Speaker
  C5 = Ceramic Capacitor [capacitance="100 nF" voltage=35V package="1206 [SMD, multilayer]"]
  C6 = Ceramic Capacitor [capacitance="100 nF" voltage=35V package="0805 [SMD, multilayer]"]
  C7 = Electrolytic Capacitor [capacitance=1µF voltage=35V package="100 mil [THT, electrolytic]"]
  R6 = Vertical Resistor [tolerance=±5% resistance=1M package=THT]
  R7 = Vertical Resistor [tolerance=±5% resistance=1M package=THT]
  LED3 = smd LED [color="Yellow (585nm)" package="0603 [SMD]"]
  LED4 = smd LED [color="Green (565nm)" package="0603 [SMD]"]
  R8 = Vertical Resistor [tolerance=±5% resistance=10k package=THT]
  R9 = Vertical Resistor [tolerance=±5% resistance=10k package=THT]

nets:
  N1: VCC1.-, CD4048B1.F, CD4048B1.VSS, Q1.3, J2.pin1, C5.1, C7.-, R7.Pin_1, LED4.cathode
  N2: VCC1.+, CD4048B1.VDD, R3.Pin_0, R9.Pin_0
  N3: CD4048B1.Kd, R6.Pin_0
  N4: CD4048B1.H, CD4048B1.G, J2.pin2
  N5: CD4048B1.E, C6.1
  N6: CD4048B1.Kb, C6.0
  N7: CD4048B1.Kc, C5.0, R6.Pin_1
  N8: CD4048B1.Ka, R8.Pin_1
  N9: CD4048B1.D, R7.Pin_0
  N10: CD4048B1.A, C2.-
  N11: Q1.1, R3.Pin_1, C2.+
  N12: Q1.2, LED3.anode
  N13: C7.+, LED4.anode, R8.Pin_0
  N14: LED3.cathode, R9.Pin_1

custom parts:
  CD4048B: CMOS Multifunction Expandable 8-Input Gate
  Transistor Top View: A standard transistor
  Vertical Resistor: A generic resistor (0.25W)
