# Fritzing sketch Versuch 3 (saved by Fritzing 0.9.6b)
breadboards: 1

parts:
  VCC1 = Battery block 9V
  CD4046 = CD4048B [part_number=CD4046BE package="DIP (Dual Inline) [THT]"]
  LED2 = LED - 5mm [color="Green (565nm)" current=0.030 package="5 mm [THT]"]
  R2 = Resistor [tolerance=±5% power=0.25 resistance=10k package=THT]

nets:
  N1: VCC1.-, CD4046.VSS, LED2.cathode
  N2: VCC1.+, CD4046.VDD
  N3: CD4046.Kd, R2.Pin_1
  N4: LED2.anode, R2.Pin_0

custom parts:
  CD4048B: CMOS Multifunction Expandable 8-Input Gate
