# Fritzing sketch Versuch 5 (saved by Fritzing 0.9.6b)
breadboards: 1

parts:
  VCC1 = Battery block 9V
  CD4046 = CD4048B [part_number=CD4046BE package="DIP (Dual Inline) [THT]"]
  R2 = Resistor [tolerance=±5% power=0.25 resistance=10k package=THT]
  LED2 = LED - 5mm [color="Green (565nm)" current=0.030 package="5 mm [THT]"]
  LED5 = LED - 5mm [color="Red (635nm)" current=0.030 package="5 mm [THT]"]
  R3 = Resistor [tolerance=±5% power=0.25 resistance=10k package=THT]

nets:
  N1: VCC1.-, CD4046.H, CD4046.VSS, LED2.cathode, LED5.cathode
  N2: VCC1.+, CD4046.VDD, R3.Pin_0
  N3: CD4046.Kd, R2.Pin_1
  N4: CD4046.A, LED5.anode, R3.Pin_1
  N5: R2.Pin_0, LED2.anode

custom parts:
  CD4048B: CMOS Multifunction Expandable 8-Input Gate
