# Fritzing sketch Versuch 6 (saved by Fritzing 0.9.6b)
breadboards: 1

parts:
  VCC1 = Battery block 9V
  CD4048B1 = CD4048B [part_number=CD4046BE package="DIP (Dual Inline) [THT]"]
  R2 = Resistor [tolerance=±5% power=0.25 resistance=10k package=THT]
  LED2 = LED - 5mm [color="Green (565nm)" current=0.030 package="5 mm [THT]"]
  LED3 = LED - 5mm [color="Yellow (592nm)" current=0.030 package="5 mm [THT]"]
  LED4 = LED - 5mm [color="Yellow (592nm)" current=0.030 package="5 mm [THT]"]

nets:
  N1: VCC1.-, CD4048B1.H, CD4048B1.VSS, LED2.cathode, LED4.anode
  N2: VCC1.+, CD4048B1.VDD, LED3.cathode
  N3: CD4048B1.Kd, R2.Pin_1
  N4: CD4048B1.A, LED3.anode, LED4.cathode
  N5: R2.Pin_0, LED2.anode

notes:
  Variante A
  Variante B

custom parts:
  CD4048B: CMOS Multifunction Expandable 8-Input Gate
