# Fritzing sketch Versuch 7 (saved by Fritzing 0.9.6b)
breadboards: 1

parts:
  VCC1 = Battery block 9V
  CD4048B1 = CD4048B [part_number=CD4046BE package="DIP (Dual Inline) [THT]"]
  LED5 = LED - 5mm [color="Red (635nm)" current=0.030 package="5 mm [THT]"]
  R3 = Resistor [tolerance=±5% power=0.25 resistance=10k package=THT]
  R5 = Vertical Resistor [tolerance=±5% resistance=10k package=THT]
  R6 = Vertical Resistor [tolerance=±5% resistance=100k package=THT]
  LED6 = LED - 5mm [color="Green (565nm)" current=0.030 package="5 mm [THT]"]

nets:
  N1: VCC1.-, CD4048B1.VSS, LED5.cathode, R6.Pin_1, LED6.cathode
  N2: VCC1.+, CD4048B1.VDD, R3.Pin_0
  N3: CD4048B1.Kd, R5.Pin_1
  N4: CD4048B1.H, LED5.anode, R3.Pin_1
  N5: CD4048B1.A, R6.Pin_0
  N6: R5.Pin_0, LED6.anode

custom parts:
  CD4048B: CMOS Multifunction Expandable 8-Input Gate
  Vertical Resistor: A generic resistor (0.25W)
