# Fritzing sketch Versuch 9 (saved by Fritzing 0.9.6b)
breadboards: 1

parts:
  VCC1 = Battery block 9V
  CD4048B1 = CD4048B [part_number=CD4046BE package="DIP (Dual Inline) [THT]"]
  LED2 = LED - 5mm [color="Green (565nm)" current=0.030 package="5 mm [THT]"]
  R1 = Resistor [tolerance=±5% power=0.25 resistance=10k package=THT]
  C2 = Ceramic Capacitor [capacitance="100 nF" voltage=35V package="0805 [SMD, multilayer]"]
  R2 = Resistor [tolerance=±5% resistance=100k package="2010 [SMD]"]
  J2 = Piezo Speaker

nets:
  N1: VCC1.-, CD4048B1.F, CD4048B1.VSS, LED2.cathode, R2.Pin_1, J2.pin1
  N2: VCC1.+, CD4048B1.Kc, CD4048B1.VDD
  N3: CD4048B1.G, R1.Pin_1, J2.pin2
  N4: CD4048B1.E, C2.1
  N5: CD4048B1.Kb, C2.0
  N6: CD4048B1.D, R2.Pin_0
  N7: LED2.anode, R1.Pin_0

custom parts:
  CD4048B: CMOS Multifunction Expandable 8-Input Gate
